# Fritzing sketch Untitled_Sketch (saved by Fritzing 0.9.3b)

parts:
  U1 = 4-Channel 5v Relay Shield [package=relay-4ch5v10a]
  Grove_LED_Red1 = Grove LED Red
  Grove_LED_Red2 = Grove LED Red
  Composant2 = Base Shield V2
  Grove_-_Bluetooth_/_BLE1 = Grove - Bluetooth / BLE
  Grove_Relay1 = Grove Relay
  Composant3 = Servo Improved

nets:
  VCC: U1.VCC, Composant2.5V
  GND: U1.GND, Composant2.GND
  N1: U1.IN1, Composant2.D7
  N2: U1.IN2, Composant2.D6_PWM
  N3: U1.IN4, Composant2.D4
  N4: U1.IN3, Composant2.D5
  N5: Grove_LED_Red1.SIG, Composant2.pin_144
  N6: Grove_LED_Red1.NC1, Composant2.pin_145
  N7: Grove_LED_Red1.NC2, Composant2.pin_146
  N8: Grove_LED_Red1.GND, Composant2.pin_147
  N9: Grove_LED_Red2.SIG, Composant2.pin_148
  N10: Grove_LED_Red2.NC1, Composant2.pin_149
  N11: Grove_LED_Red2.NC2, Composant2.pin_150
  N12: Grove_LED_Red2.GND, Composant2.pin_151
  N13: Composant2.pin_96, Grove_-_Bluetooth_/_BLE1.GND
  N14: Composant2.pin_97, Grove_-_Bluetooth_/_BLE1.VCC
  N15: Composant2.pin_98, Grove_-_Bluetooth_/_BLE1.Tx
  N16: Composant2.pin_99, Grove_-_Bluetooth_/_BLE1.Rx
  N17: Composant2.pin_120, Composant3.ground
  N18: Composant2.pin_121, Composant3.vcc
  N19: Composant2.pin_123, Composant3.signal
  N20: Composant2.pin_140, Grove_Relay1.SIG
  N21: Composant2.pin_141, Grove_Relay1.NC
  N22: Composant2.pin_142, Grove_Relay1.VCC
  N23: Composant2.pin_143, Grove_Relay1.GND

custom parts:
  4-Channel 5v Relay Shield: 4 Channel 5v Relay Shield w. 2x SPD-06VDC-SD-C
  Grove LED Red: LED red, Grove connector.
  Grove Relay: Relay, Grove connector.
